# Fritzing sketch lab_1 (saved by Fritzing 0.9.2b)
breadboards: 1

parts:
  Part1 = Arduino Uno (Rev3)
  LED1 = LED - 5mm [color="Red (633nm)" package="5 mm [THT]"]
  LED2 = LED - 5mm [color="Red (633nm)" package="5 mm [THT]"]
  R1 = Resistor [tolerance=±5% resistance=560 package=THT]
  R2 = Resistor [tolerance=±5% resistance=560 package=THT]

nets:
  N1: Part1.5V, R1.Pin_1, R2.Pin_1
  N2: LED1.anode, R2.Pin_0
  N3: LED2.anode, R1.Pin_0
